// Logisim project BancDeRegistres.circ as structural Verilog: 2 circuits, main circuit BancRegistre
module BancRegistre (
  input  [31:0] DataIn,
  input  [2:0] RegA,
  input  [2:0] RegB,
  input  [2:0] RegDest,
  input  Clk,
  input  Reset,
  output [31:0] AOut,
  output [31:0] BOut
);

  wire decoder_1_out0, decoder_1_out1, decoder_1_out2, decoder_1_out3, decoder_1_out4, decoder_1_out5,
       decoder_1_out6, decoder_1_out7;
  wire [31:0] register_1_q, register_2_q, register_3_q, register_4_q, register_5_q, register_6_q,
       register_7_q, register_8_q;

  Decoder #(.select(3)) decoder_1 (
    .out0(decoder_1_out0), .out1(decoder_1_out1), .out2(decoder_1_out2), .out3(decoder_1_out3),
    .out4(decoder_1_out4), .out5(decoder_1_out5), .out6(decoder_1_out6), .out7(decoder_1_out7), .sel(RegDest));  // open: en
  Multiplexer #(.select(3), .width(32)) multiplexer_1 (
    .in0(register_1_q), .in1(register_2_q), .in2(register_3_q), .in3(register_4_q), .in4(register_5_q),
    .in5(register_6_q), .in6(register_7_q), .in7(register_8_q), .out(AOut), .sel(RegA));
  Multiplexer #(.select(3), .width(32)) multiplexer_2 (
    .in0(register_1_q), .in1(register_2_q), .in2(register_3_q), .in3(register_4_q), .in4(register_5_q),
    .in5(register_6_q), .in6(register_7_q), .in7(register_8_q), .out(BOut), .sel(RegB));
  Register #(.width(32)) register_1 (.D(DataIn), .en(decoder_1_out0), .clk(Clk), .Q(register_1_q), .clr(Reset));
  Register #(.width(32)) register_2 (.D(DataIn), .en(decoder_1_out1), .clk(Clk), .Q(register_2_q), .clr(Reset));
  Register #(.width(32)) register_3 (.D(DataIn), .en(decoder_1_out2), .clk(Clk), .Q(register_3_q), .clr(Reset));
  Register #(.width(32)) register_4 (.D(DataIn), .en(decoder_1_out3), .clk(Clk), .Q(register_4_q), .clr(Reset));
  Register #(.width(32)) register_5 (.D(DataIn), .en(decoder_1_out4), .clk(Clk), .Q(register_5_q), .clr(Reset));
  Register #(.width(32)) register_6 (.D(DataIn), .en(decoder_1_out5), .clk(Clk), .Q(register_6_q), .clr(Reset));
  Register #(.width(32)) register_7 (.D(DataIn), .en(decoder_1_out6), .clk(Clk), .Q(register_7_q), .clr(Reset));
  Register #(.width(32)) register_8 (.D(DataIn), .en(decoder_1_out7), .clk(Clk), .Q(register_8_q), .clr(Reset));
endmodule

module Testing (
  input  [31:0] in_1,
  input  [2:0] in_2,
  input  in_3,
  input  [2:0] in_4,
  input  [2:0] in_5,
  output [31:0] out_6,
  output [31:0] out_7
);

  wire clock_1_out;

  Clock clock_1 (.out(clock_1_out));
  BancRegistre bancregistre_1 (
    .RegDest(in_2), .DataIn(in_1), .Clk(clock_1_out), .Reset(in_3), .RegA(in_4), .RegB(in_5), .AOut(out_7),
    .BOut(out_6));
endmodule
