// Logisim project Ctl_Shift_Add_Sub_Mov.circ as structural Verilog: 1 circuit, main circuit Shift_Add_Sub_Mov
module Shift_Add_Sub_Mov (
  input  Enable,
  input  [15:0] Instruction,
  output [3:0] Flags_Update_Mask,
  output Carry,
  output Imm32_Enable,
  output [2:0] Rm,
  output [2:0] Rn,
  output [2:0] Rd,
  output [4:0] Imm5,
  output [31:0] Imm32,
  output [3:0] ALU_Opcode
);

  wire and_1_out, and_2_out, and_3_out, and_4_out, and_5_out, and_6_out, and_7_out, and_8_out, and_9_out,
       and_10_out, and_11_out;
  wire [3:0] priority_encoder_1_out;

  Multiplexer #(.width(3)) multiplexer_1 (
    .in0(Instruction[2:0]), .in1(Instruction[10:8]), .out(Rd), .sel(Instruction[13]));
  and and_1 (and_1_out, ~Instruction[13], ~Instruction[12], ~Instruction[11]);  // AND_Gate
  and and_2 (and_2_out, ~Instruction[13], ~Instruction[12], Instruction[11]);  // AND_Gate
  and and_3 (and_3_out, ~Instruction[13], Instruction[12], ~Instruction[11]);  // AND_Gate
  and and_4 (and_4_out, ~Instruction[13], Instruction[12], Instruction[11], ~Instruction[10], ~Instruction[9]);  // AND_Gate
  and and_5 (and_5_out, ~Instruction[13], Instruction[12], Instruction[11], ~Instruction[10], Instruction[9]);  // AND_Gate
  and and_6 (and_6_out, ~Instruction[13], Instruction[12], Instruction[11], Instruction[10], ~Instruction[9]);  // AND_Gate
  and and_7 (and_7_out, ~Instruction[13], Instruction[12], Instruction[11], Instruction[10], Instruction[9]);  // AND_Gate
  and and_8 (and_8_out, Instruction[13], ~Instruction[12], ~Instruction[11]);  // AND_Gate
  and and_9 (and_9_out, Instruction[13], ~Instruction[12], Instruction[11]);  // AND_Gate
  and and_10 (and_10_out, Instruction[13], Instruction[12], ~Instruction[11]);  // AND_Gate
  and and_11 (and_11_out, Instruction[13], Instruction[12], Instruction[11]);
  Priority_Encoder #(.select(4)) priority_encoder_1 (
    .in0(and_1_out), .in1(and_2_out), .in2(and_3_out), .in3(and_4_out), .in4(and_5_out), .in5(and_6_out),
    .in6(and_7_out), .in7(and_8_out), .in8(and_9_out), .in9(and_10_out), .in10(and_11_out),
    .out(priority_encoder_1_out));  // open: in11, in12, in13, in14, in15, gs, en_out, en_in
  Multiplexer #(.select(4), .width(4)) multiplexer_2 (
    .in0(4'b0010), .in1(4'b0011), .in2(4'b0100), .in3(4'b0101), .in4(4'b0110), .in5(4'b0101), .in6(4'b0110),
    .in7(4'b1001), .in8(4'b1010), .in9(4'b0101), .in10(4'b0110), .out(ALU_Opcode),
    .sel(priority_encoder_1_out));  // open: in11, in12, in13, in14, in15

  // Other names for the same wires on the sheet: b13 = Instruction[13]; RdMux[2:0] = Rd

  // Notes on the sheet:
  //   Note: ALU uses Rn register for shifts. Use Rn instead of Rm for shifts (immediate) here too
  //   Note 3: Imm32_Enable forces the use of the immediate for Rm register
  //   Note 2: MOV uses RSB ALU opcode with Imm8 reversed so that it is copied to output register
  //   Pull output low on Enable = 0
  //   only ADD and SUB use Rm
  //   Enable carry for SUB since it is reversed in ALU
  //   ALU will use Imm32 instead of Rm
endmodule
